# Fritzing sketch tdos-arduino-prototype (saved by Fritzing 0.9.2b)
breadboards: 2

parts:
  Part1 = Arduino Nano (Rev3.0)
  OLED = Grove OLED 128x96
  MCP3008 = SO16 [chip_label=SO16 package=SO]  # not connected
  R3 = Trimmer Potentiometer [maximum_resistance=10kΩ package=THT]
  U1 = Optocoupler [package=THT]
  R4 = Trimmer Potentiometer [maximum_resistance=10kΩ package=THT]
  220k = Resistor [tolerance=±5% resistance=220 package="2512 [SMD]"]
  LED1 = smd LED [color="Red (633nm)" package="0603 [SMD]"]
  1k = Resistor [tolerance=±5% resistance=220 package="2512 [SMD]"]

nets:
  GND: Part1.GND, OLED.GND, R3.leg1
  N1: Part1.5V, R3.leg2, R4.leg2, 220k.Pin_0, 1k.Pin_1
  N2: Part1.A5, OLED.SCL
  N3: Part1.A4, OLED.SDA
  N4: Part1.A0, R4.wiper
  3V3: Part1.3V3, OLED.VCC
  N5: U1.Pin_1, 1k.Pin_0
  N6: U1.Pin_5, LED1.anode
  N7: 220k.Pin_1, LED1.cathode

notes:
  MCP3008
  OLED
  follow your
  pin description,
  not the layout
  R_A0
  R_M0
